// Digital circuit DesEsquerda.dig as structural Verilog
module DesEsquerda (
  input  [31:0] A,
  input  [31:0] B,
  output [31:0] S
);

  BarrelShifter #(.Bits(32)) barrelshifter_1 (.in(A), .shift(B[5:0]), .out(S));
endmodule
