// Digital circuit SomaBits.dig as structural Verilog
module SomaBits (
  input  Cin,
  input  [3:0] A,
  input  [3:0] B,
  output [3:0] S,
  output Co
);

  wire and_1_out, and_2_out, and_3_out, and_4_out, and_5_out, and_6_out, and_7_out, and_8_out, and_9_out,
       and_10_out, and_11_out, and_12_out, and_13_out, and_14_out, or_1_out, or_2_out, or_3_out, xor_1_out,
       xor_3_out, xor_5_out, xor_7_out;

  and and_1 (and_1_out, A[0], B[0]);
  xor xor_1 (xor_1_out, A[0], B[0]);
  xor xor_2 (S[0], Cin, xor_1_out);
  and and_2 (and_2_out, A[1], B[1]);
  and and_3 (and_3_out, xor_1_out, Cin);
  xor xor_3 (xor_3_out, A[1], B[1]);
  or or_1 (or_1_out, and_1_out, and_3_out);
  xor xor_4 (S[1], or_1_out, xor_3_out);
  and and_4 (and_4_out, A[2], B[2]);
  xor xor_5 (xor_5_out, A[2], B[2]);
  and and_5 (and_5_out, Cin, xor_1_out, xor_3_out);
  and and_6 (and_6_out, and_1_out, xor_3_out);
  or or_2 (or_2_out, and_5_out, and_6_out, and_2_out);
  xor xor_6 (S[2], or_2_out, xor_5_out);
  and and_7 (and_7_out, A[3], B[3]);
  xor xor_7 (xor_7_out, A[3], B[3]);
  and and_8 (and_8_out, Cin, xor_1_out, xor_3_out, xor_5_out);
  and and_9 (and_9_out, and_1_out, xor_3_out, xor_5_out);
  and and_10 (and_10_out, and_2_out, xor_5_out);
  and and_11 (and_11_out, Cin, xor_1_out, xor_3_out, xor_5_out, xor_7_out);
  and and_12 (and_12_out, and_1_out, xor_3_out, xor_5_out, xor_7_out);
  and and_13 (and_13_out, and_2_out, xor_5_out, xor_7_out);
  and and_14 (and_14_out, and_4_out, xor_7_out);
  or or_3 (or_3_out, and_8_out, and_9_out, and_10_out, and_4_out);
  or or_4 (Co, and_11_out, and_12_out, and_7_out, and_13_out, and_14_out);
  xor xor_8 (S[3], or_3_out, xor_7_out);
endmodule
