// Digital circuit Somador24.dig as structural Verilog
module Somador24 (
  input  [23:0] A,
  input  [23:0] B,
  output [23:0] S
);

  wire somabits_1_co, somabits_2_co, somabits_3_co, somabits_4_co, somabits_5_co;

  SomaBits somabits_1 (.Cin(1'b0), .A(A[3:0]), .B(B[3:0]), .S(S[3:0]), .Co(somabits_1_co));
  SomaBits somabits_2 (.Cin(somabits_1_co), .A(A[7:4]), .B(B[7:4]), .S(S[7:4]), .Co(somabits_2_co));
  SomaBits somabits_3 (.Cin(somabits_2_co), .A(A[11:8]), .B(B[11:8]), .S(S[11:8]), .Co(somabits_3_co));
  SomaBits somabits_4 (.Cin(somabits_3_co), .A(A[15:12]), .B(B[15:12]), .S(S[15:12]), .Co(somabits_4_co));
  SomaBits somabits_5 (.Cin(somabits_4_co), .A(A[19:16]), .B(B[19:16]), .S(S[19:16]), .Co(somabits_5_co));
  SomaBits somabits_6 (.Cin(somabits_5_co), .A(A[23:20]), .B(B[23:20]), .S(S[23:20]));  // open: Co

  // Other names for the same wires on the sheet: S0[3:0] = S[3:0]; S1[3:0] = S[7:4]; S2[3:0] = S[11:8];
  //   S3[3:0] = S[15:12]; S4[3:0] = S[19:16]; S5[3:0] = S[23:20]
endmodule
