// Digital circuit ULA.dig as structural Verilog
module ULA (
  input  [31:0] A,
  input  [31:0] B,
  input  [2:0] C,
  output [31:0] S,
  output Z
);

  wire [31:0] and_1_out, desdireita_1_s, desesquerda_1_s, not_1_out, or_1_out, somadorlook_1_s,
       subtrator_1_s, xor_1_out;

  SomadorLook somadorlook_1 (.A(A), .B(B), .S(somadorlook_1_s));
  Subtrator subtrator_1 (.A(A), .B(B), .S(subtrator_1_s));
  assign and_1_out = A & B;  // And and_1, 32 bits wide
  assign or_1_out = A | B;  // Or or_1, 32 bits wide
  assign xor_1_out = A ^ B;  // XOr xor_1, 32 bits wide
  assign not_1_out = ~A;  // Not not_1, 32 bits wide
  DesEsquerda desesquerda_1 (.A(A), .B(B), .S(desesquerda_1_s));
  DesDireita desdireita_1 (.A(A), .B(B), .S(desdireita_1_s));
  Multiplexer #(.Selector_Bits(3), .Bits(32)) multiplexer_1 (
    .sel(C), .in_0(somadorlook_1_s), .in_1(subtrator_1_s), .in_2(and_1_out), .in_3(or_1_out),
    .in_4(xor_1_out), .in_5(not_1_out), .in_6(desesquerda_1_s), .in_7(desdireita_1_s), .out(S));
  Zero zero_1 (.IN(S), .S(Z));
  // Probe on Z
endmodule
