// Digital circuit Display.dig as structural Verilog
module Display (
  input  [31:0] a,
  input  e,
  output [31:0] S
);

  Multiplexer #(.Bits(32)) multiplexer_1 (.sel(e), .in_0({32{1'b0}}), .in_1(a), .out(S));
endmodule
