// Digital circuit Subtrator.dig as structural Verilog
module Subtrator (
  input  [31:0] A,
  input  [31:0] B,
  output [31:0] S
);

  wire [31:0] not_1_out, somadorlook_1_s;

  assign not_1_out = ~B;  // Not not_1, 32 bits wide
  SomadorLook somadorlook_1 (.A(32'h1), .B(not_1_out), .S(somadorlook_1_s));
  SomadorLook somadorlook_2 (.A(A), .B(somadorlook_1_s), .S(S));
endmodule
