// Digital circuit Trabalho.dig as structural Verilog
module Trabalho (
  input  clk
);

  wire and_1_out, Branch, Enable, Halt, Muxip, Muxula, or_1_out, Write, zero;
  wire [2:0] Ula;
  wire [23:0] bitextender_1_out, IP_q, multiplexer_1_out, multiplexer_2_out, somador24_1_s;
  wire [31:0] display_1_s, multiplexer_3_out, Programa_d, registrador32_1_a_2, registrador32_1_b_2, ula_1_s,
       unsigned_1_s;

  BitExtender #(.inputBits(16), .outputBits(24)) bitextender_1 (.in(Programa_d[15:0]), .out(bitextender_1_out));
  Multiplexer #(.Bits(24)) multiplexer_1 (
    .sel(or_1_out), .in_0(24'h1), .in_1(bitextender_1_out), .out(multiplexer_1_out));
  or or_1 (or_1_out, Muxip, and_1_out);
  Multiplexer #(.Bits(24)) multiplexer_2 (
    .sel(Halt), .in_0(multiplexer_1_out), .in_1({24{1'b0}}), .out(multiplexer_2_out));
  and and_1 (and_1_out, zero, Branch);
  Somador24 somador24_1 (.A(IP_q), .B(multiplexer_2_out), .S(somador24_1_s));
  D_FF #(.Bits(24)) IP (.D(somador24_1_s), .C(clk), .Q(IP_q));  // open: nQ
  // Probe on IP_q
  ROM #(.AddrBits(24), .Bits(32)) Programa (.A(IP_q), .sel(1'b1), .D(Programa_d));
  ROM #(.AddrBits(4), .Bits(9)) Controle (
    .A(Programa_d[31:28]), .sel(1'b1), .D({Halt, Branch, Muxula, Ula, Write, Enable, Muxip}));
  Registrador32 registrador32_1 (
    .C(ula_1_s), .a(Programa_d[27:24]), .b(Programa_d[23:20]), .c_2(Programa_d[19:16]), .W(Write),
    .Clock(clk), .A_2(registrador32_1_a_2), .B_2(registrador32_1_b_2));
  Unsigned unsigned_1 (.E(Programa_d[15:0]), .S(unsigned_1_s));
  // Probe on registrador32_1_a_2
  // Probe on registrador32_1_b_2
  Multiplexer #(.Bits(32)) multiplexer_3 (
    .sel(Muxula), .in_0(registrador32_1_b_2), .in_1(unsigned_1_s), .out(multiplexer_3_out));
  Display display_1 (.a(registrador32_1_a_2), .e(Enable), .S(display_1_s));
  // Probe on display_1_s
  ULA ula_1 (.A(registrador32_1_a_2), .B(multiplexer_3_out), .C(Ula), .S(ula_1_s), .Z(zero));
  // Probe on ula_1_s
  // Probe on zero

  // Other names for the same wires on the sheet: Clock = clk

  // Notes on the sheet:
  //   contents of Programa (hex, n*v repeats v):
  //   0,b0010015,b0020003,11230000,c3000000,21240000,c4000000,31250000
  //   ,c5000000,41260000,c6000000,51270000,c7000000,61080000,c8000000
  //   ,71290000,c9000000,812a0000,ca000000,d0000004,0,0,0,910b0004,cb000000
  //   ,a10c0004,cc000000,b00d0015,21de0000,e0000003,0,0,f0000000
  //   contents of Controle (hex, n*v repeats v):
  //   0,4,c,14,1c,24,2c,34,3c,5c,64,44,2,1,d,101
endmodule
