// Digital circuit Zero.dig as structural Verilog
module Zero (
  input  [31:0] IN,
  output S
);

  wire or_1_out;

  or or_1 (or_1_out, IN[31], IN[30], IN[29], IN[28], IN[27], IN[26], IN[25], IN[24], IN[23], IN[22], IN[21], IN[20], IN[19], IN[18], IN[17], IN[16], IN[15], IN[14], IN[13], IN[12], IN[11], IN[10], IN[9], IN[8], IN[7], IN[6], IN[5], IN[4], IN[3], IN[2], IN[1], IN[0]);
  not not_1 (S, or_1_out);
  // Probe on S

  // Other names for the same wires on the sheet: _1 = IN[0]; _2 = IN[1]; _3 = IN[2]; _4 = IN[3]; _5 = IN[4];
  //   _6 = IN[5]; _7 = IN[6]; _8 = IN[7]; _9 = IN[8]; _10 = IN[9]; _11 = IN[10]; _12 = IN[11]; _13 = IN[12];
  //   _14 = IN[13]; _15 = IN[14]; _16 = IN[15]; _17 = IN[16]; _18 = IN[17]; _19 = IN[18]; _20 = IN[19]; _21 = IN[20];
  //   _22 = IN[21]; _23 = IN[22]; _24 = IN[23]; _25 = IN[24]; _26 = IN[25]; _27 = IN[26]; _28 = IN[27]; _29 = IN[28];
  //   _30 = IN[29]; _31 = IN[30]; _32 = IN[31]
endmodule
